# Fritzing sketch Bienenwaage 5.0 TTGO-T-CALL (saved by Fritzing 0.9.3b)
circuit board: 10cm x 8cm
breadboards: 1

parts:
  4_7kΩ = Resistor [tolerance=±5% resistance=4.7k package=THT]
  Sensor1 = screw terminal, 3 pins
  HX711 = HX711 my Weighing Sensor Module
  Waage_2 = screw terminal, 5 pins
  Waage_1 = screw terminal, 5 pins
  Sensor2 = screw terminal, 3 pins
  +_LiPo_- = Screw terminal - 2 pins [package=THT]
  Solar_-_+ = Screw terminal - 2 pins [package=THT]
  HX711_2 = HX711 my Weighing Sensor Module
  TP1 = TP4056 [chip_label=TP4056 package="DIP (Dual Inline) [THT]"]
  Power4TTGO = Screw terminal - 2 pins [package=THT]
  Mod1 = TTGO-T-Call-V1.3-ESP32 [package=THT]
  JST_Anschluß_TTGO-T-CALL = female pin header, 2 pins [form="♀ (female)"]

nets:
  N1: 4_7kΩ.Pin_0, Sensor1.pin2, Sensor2.pin2, Mod1.19
  N2: 4_7kΩ.Pin_1, Sensor1.pin3, Sensor2.pin3, TP1.pin3, Power4TTGO.pin1, JST_Anschluß_TTGO-T-CALL.pin1
  N3: Sensor1.pin1, HX711.GND#5, Waage_2.pin1, Waage_1.pin1, Sensor2.pin1, HX711_2.GND#5, TP1.pin6, Power4TTGO.pin2, Mod1.GND, JST_Anschluß_TTGO-T-CALL.pin2
  VCC: HX711.VCC, HX711_2.VCC, Mod1.5V
  N4: HX711.DO/RX, Mod1.33
  N5: HX711.CK/TX, Mod1.32
  N6: HX711.out+, Waage_1.pin2
  N7: HX711.A-, Waage_1.pin3
  N8: HX711.A+, Waage_1.pin4
  N9: HX711.GND#14, Waage_1.pin5
  N10: Waage_2.pin2, HX711_2.GND#14
  N11: Waage_2.pin3, HX711_2.A+
  N12: Waage_2.pin4, HX711_2.A-
  N13: Waage_2.pin5, HX711_2.out+
  N14: +_LiPo_-.pin1, TP1.pin4
  N15: +_LiPo_-.pin2, TP1.pin5
  N16: Solar_-_+.pin1, TP1.pin2
  N17: Solar_-_+.pin2, TP1.pin1
  N18: HX711_2.DO/RX, Mod1.14
  N19: HX711_2.CK/TX, Mod1.25

notes:
  VCC
  Data
  shield
  E+A-A+E-
  GND
  Vcc
  out+
  A-
  A+
  CLK/Tx
  Do/Rx
  E-A+A-E+
  Bienenwaage 5.0 TTGO-T-CALL

custom parts:
  HX711 my Weighing Sensor Module: HX711 is a precision 24-bit analog-to-digital converter (ADC) designed for weigh scales and industrial control applications to interface directly with a bridge sensor.
  TP4056: A DIP stand-in part for whatever IC you want. With 6 pins on a 300mil dual inline package (DIP) footprint.
  TTGO-T-Call-V1.3-ESP32: LILYGO® TTGO T-Call V1.3 ESP32 Wireless Module GPRS Antenna SIM Card SIM800L Module
